// Logisim project PipelinedCore.circ as structural Verilog: 15 circuits, main circuit RVI 1cycle
module RVI_1cycle (
);

  wire alu_abstraction_1_branch, ALUBSrc, ALUSrc, ALUSrcID, branch_alu_1_branchaluoutput, BranchID, clk,
       DoBranch, ex_mem_1_zero_2, id_ex_1_memwrite_2, IFIDFlushtoStall, IFIDWrite, main_control_1_memwrite,
       main_control_1_pcjumpsrc, main_control_1_regwrite, MemRead, MemReadEX, MemReadID, MemWrite,
       MemWriteID, multiplexer_2_out, or_2_out, PCSrc, PCSrcBranch, PCWrite, RegWrite, RegWriteEX,
       RegWriteID, RegWriteMEM, rst, Stall, undriven_2;
  wire [0:0] adder_2_out_2;
  wire [1:0] ex_mem_1_writedatasrc_2, ForwardALUA, ForwardALUB, forwarding_1_forwarda, forwarding_1_forwardb,
       id_ex_1_writedatasrc_2, LuiAuipcSel, LuiAuipcSelID, WriteDataSrc, WriteDataSrcID;
  wire [2:0] id_ex_1_storeloadsel_2, StoreLoadSel, StoreLoasSelID;
  wire [3:0] store_1_memorybytesel;
  wire [4:0] ALUCtrl, ALUCtrlID, EXRd, EXRs1, EXRs2, MEMRd, Rs1, Rs2, WBRd;
  wire [7:0] PC_q_2;
  wire [30:0] adder_2_out;
  wire [31:0] adder_1_out, alu_abstraction_1_aluoutput, ex_mem_1_pc_2, ex_mem_1_readdata2_2,
       id_ex_1_immediate_2, id_ex_1_instruction_2, id_ex_1_pc_2, id_ex_1_readdata1_2, id_ex_1_readdata2_2,
       if_id_1_instruction_2, if_id_1_pc_2, Immediate, load_1_fixeddata, mem_wb_1_aluoutput_2,
       mem_wb_1_dataoutput_2, mem_wb_1_pc_2, MEMWriteData, multiplexer_1_out, multiplexer_3_out,
       multiplexer_6_out, multiplexer_7_out, multiplexer_8_out, multiplexer_9_out, multiplexer_10_out,
       multiplexer_11_out, PC_q, ram_1_data, ReadData1, ReadData2, rom_1_data, store_1_fixeddata, undriven,
       WBPCPlus4, WriteData;

  Clock u_clk (.out(clk));
  Button Reset_Regs (.out(rst));
  Multiplexer #(.width(32), .enable("false")) multiplexer_1 (
    .in0(adder_1_out), .in1({adder_2_out, 1'b0}), .out(multiplexer_1_out), .sel(PCSrc));
  Register #(.width(32)) PC (
    .D(multiplexer_1_out), .en(PCWrite), .Q({PC_q[31:10], PC_q_2, PC_q[1:0]}), .clk(clk), .clr(rst));
  or or_1 (PCSrc, WriteDataSrcID[1], PCSrcBranch);
  Adder #(.width(32)) adder_1 (.a(32'h4), .b({PC_q[31:10], PC_q_2, PC_q[1:0]}), .out(adder_1_out));  // open: cin, cout
  Multiplexer #(.enable("false")) multiplexer_2 (
    .in0(IFIDFlushtoStall), .in1(1'b0), .out(multiplexer_2_out), .sel(Stall));
  ROM #(.dataWidth(32)) rom_1 (.addr(PC_q_2), .data(rom_1_data));  // open: sel
  IF_ID if_id_1 (
    .clk(clk), .rst(or_2_out), .Instruction(rom_1_data), .PC({PC_q[31:10], PC_q_2, PC_q[1:0]}),
    .Instruction_2({if_id_1_instruction_2[31:25], Rs2, Rs1, if_id_1_instruction_2[14:0]}),
    .PC_2(if_id_1_pc_2), .en(IFIDWrite));
  or or_2 (or_2_out, multiplexer_2_out, rst);
  // Probe on {if_id_1_instruction_2[31:25], Rs2, Rs1, if_id_1_instruction_2[14:0]}
  Main_Control main_control_1 (
    .Instruction({if_id_1_instruction_2[31:25], Rs2, Rs1, if_id_1_instruction_2[14:0]}), .ALUSrc(ALUSrcID),
    .WriteDataSrc(WriteDataSrcID), .RegWrite(main_control_1_regwrite), .MemRead(MemReadID),
    .MemWrite(main_control_1_memwrite), .DoJump(DoBranch), .ALUCtrl(ALUCtrlID),
    .PCJumpSrc(main_control_1_pcjumpsrc), .LuiAuipcSel(LuiAuipcSelID), .StoreLoadSel(StoreLoasSelID));
  ImmGen immgen_1 (
    .Instruction({if_id_1_instruction_2[31:25], Rs2, Rs1, if_id_1_instruction_2[14:0]}), .Immediate(Immediate));
  Forwarding forwarding_1 (
    .Rs1(Rs1), .MEMRd(MEMRd), .WBRd(WBRd), .Rs2(Rs2), .RegWriteMEM(RegWriteMEM), .RegWrite(RegWrite),
    .ForwardA(forwarding_1_forwarda), .ForwardB(forwarding_1_forwardb));
  Multiplexer #(.select(2), .width(32), .enable("false")) multiplexer_3 (
    .in0(ReadData1), .in1(MEMWriteData), .in2(WriteData), .out(multiplexer_3_out), .sel(forwarding_1_forwarda));  // open: in3
  Multiplexer #(.enable("false")) multiplexer_4 (
    .in0(main_control_1_regwrite), .in1(1'b0), .out(RegWriteID), .sel(Stall));
  Multiplexer #(.enable("false")) multiplexer_5 (
    .in0(main_control_1_memwrite), .in1(1'b0), .out(MemWriteID), .sel(Stall));
  Multiplexer #(.width(32), .enable("false")) multiplexer_6 (
    .in0(if_id_1_pc_2), .in1(ReadData1), .out(multiplexer_6_out), .sel(main_control_1_pcjumpsrc));
  // Probe on Immediate
  Hazard_Detection hazard_detection_1 (
    .PCWrite(PCWrite), .MemReadEX(MemReadEX), .IFIDWrite(IFIDWrite),
    .Instruction({if_id_1_instruction_2[31:25], Rs2, Rs1, if_id_1_instruction_2[14:0]}), .Stall(Stall),
    .IFIDFlush(IFIDFlushtoStall), .EXRd(EXRd), .PCSrc(PCSrc), .MemRead(MemRead), .BranchID(BranchID),
    .MEMRd(MEMRd), .RegWriteEX(RegWriteEX));
  Adder #(.width(32)) adder_2 (
    .a(multiplexer_6_out), .b(Immediate), .out({adder_2_out, adder_2_out_2[0]}));  // open: cin, cout
  Register_File register_file_1 (
    .clk(clk), .rst(rst), .ReadData1(ReadData1), .ReadData2(ReadData2), .WriteEn(RegWrite), .Rd(WBRd),
    .WriteData(WriteData), .Rs1(Rs1), .Rs2(Rs2));
  // Probe on ReadData1
  // Probe on ReadData2
  Multiplexer #(.select(2), .width(32), .enable("false")) multiplexer_7 (
    .in0(ReadData2), .in1(MEMWriteData), .in2(WriteData), .in3(undriven), .out(multiplexer_7_out),
    .sel(forwarding_1_forwardb));
  Branch_ALU branch_alu_1 (
    .BranchALUOutput(branch_alu_1_branchaluoutput), .BranchA(multiplexer_3_out), .BranchB(multiplexer_7_out),
    .ALUCtrl(ALUCtrlID));
  and and_1 (PCSrcBranch, branch_alu_1_branchaluoutput, DoBranch);
  ID_EX id_ex_1 (
    .clk(clk), .rst(rst), .ReadData1(ReadData1), .ReadData1_2(id_ex_1_readdata1_2), .ReadData2(ReadData2),
    .ReadData2_2(id_ex_1_readdata2_2), .Immediate(Immediate), .Immediate_2(id_ex_1_immediate_2),
    .PC(if_id_1_pc_2), .PC_2(id_ex_1_pc_2),
    .Instruction({if_id_1_instruction_2[31:25], Rs2, Rs1, if_id_1_instruction_2[14:0]}),
    .Instruction_2(id_ex_1_instruction_2), .Rd(if_id_1_instruction_2[11:7]), .Rd_2(EXRd), .ALUSrc(ALUSrcID),
    .ALUSrc_2(ALUSrc), .ALUCtrl(ALUCtrlID), .ALUCtrl_2(ALUCtrl), .StoreLoadSel(StoreLoasSelID),
    .StoreLoadSel_2(id_ex_1_storeloadsel_2), .MemWrite(MemWriteID), .MemWrite_2(id_ex_1_memwrite_2),
    .MemRead(MemReadID), .MemRead_2(MemReadEX), .RegWrite(RegWriteID), .RegWrite_2(RegWriteEX),
    .ReadDir1(Rs1), .ReadDir1_2(EXRs1), .ReadDir2(Rs2), .ReadDir2_2(EXRs2), .LuiAuipcSel(LuiAuipcSelID),
    .LuiAuipcSel_2(LuiAuipcSel), .WriteDataSrc(WriteDataSrcID), .WriteDataSrc_2(id_ex_1_writedatasrc_2));
  Multiplexer #(.select(2), .width(32), .enable("false")) multiplexer_8 (
    .in0(id_ex_1_readdata1_2), .in2(MEMWriteData), .in3(WriteData), .out(multiplexer_8_out), .sel(ForwardALUA));  // open: in1
  Multiplexer #(.select(2), .width(32), .enable("false")) multiplexer_9 (
    .in0(id_ex_1_readdata2_2), .in1(MEMWriteData), .in2(WriteData), .out(multiplexer_9_out), .sel(ForwardALUB));  // open: in3
  Forwarding forwarding_2 (
    .Rs1(EXRs1), .MEMRd(MEMRd), .WBRd(WBRd), .Rs2(EXRs2), .RegWriteMEM(RegWriteMEM), .RegWrite(RegWrite),
    .ForwardA(ForwardALUA), .ForwardB(ForwardALUB));
  Multiplexer #(.select(2), .width(32), .enable("false")) multiplexer_10 (
    .in0(multiplexer_8_out), .in1({32{1'b0}}), .in2(id_ex_1_pc_2), .out(multiplexer_10_out), .sel(LuiAuipcSel));  // open: in3
  Multiplexer #(.width(32), .enable("false")) multiplexer_11 (
    .in0(multiplexer_9_out), .in1(id_ex_1_immediate_2), .out(multiplexer_11_out), .sel(ALUBSrc));
  // Probe on undriven_2
  ALU_Abstraction alu_abstraction_1 (
    .ALUOutput(alu_abstraction_1_aluoutput), .Branch(alu_abstraction_1_branch), .ALUA(multiplexer_10_out),
    .ALUB(multiplexer_11_out), .ALUCtrl(ALUCtrl));
  // Probe on multiplexer_9_out
  EX_MEM ex_mem_1 (
    .clk(clk), .rst(rst), .PC(id_ex_1_pc_2), .PC_2(ex_mem_1_pc_2), .Zero(alu_abstraction_1_branch),
    .Zero_2(ex_mem_1_zero_2), .ALUOutput(alu_abstraction_1_aluoutput), .ALUOutput_2(MEMWriteData),
    .ReadData2(multiplexer_9_out), .ReadData2_2(ex_mem_1_readdata2_2), .Rd(EXRd), .Rd_2(MEMRd),
    .RegWrite(RegWriteEX), .RegWrite_2(RegWriteMEM), .MemWrite(id_ex_1_memwrite_2), .MemWrite_2(MemWrite),
    .MemRead(MemReadEX), .MemRead_2(MemRead), .WriteDataSrc(id_ex_1_writedatasrc_2),
    .WriteDataSrc_2(ex_mem_1_writedatasrc_2), .StoreLoadSel(id_ex_1_storeloadsel_2),
    .StoreLoadSel_2(StoreLoadSel));
  Store store_1 (
    .Data(ex_mem_1_readdata2_2), .FixedData(store_1_fixeddata), .MemoryByteSel(store_1_memorybytesel),
    .AluOutput(StoreLoadSel[1:0]), .DataType(MEMWriteData[1:0]));
  RAM #(.dataWidth(32), .bus("separate")) ram_1 (
    .addr(MEMWriteData[9:2]), .din(store_1_fixeddata), .data(ram_1_data), .str(MemWrite), .clk(clk),
    .ld(MemRead));  // open: sel, clr
  // Probe on MEMWriteData
  Load load_1 (
    .Data(ram_1_data), .FixedData(load_1_fixeddata), .DataType(StoreLoadSel[1:0]),
    .Unsigned(StoreLoadSel[2]), .AluOutput(MEMWriteData[1:0]));
  MEM_WB mem_wb_1 (
    .clk(clk), .rst(rst), .ALUOutput(MEMWriteData), .ALUOutput_2(mem_wb_1_aluoutput_2),
    .DataOutput(load_1_fixeddata), .DataOutput_2(mem_wb_1_dataoutput_2), .WriteDir(MEMRd), .WriteDir_2(WBRd),
    .RegWrite(RegWriteMEM), .RegWrite_2(RegWrite), .WriteDataSrc(ex_mem_1_writedatasrc_2),
    .WriteDataSrc_2(WriteDataSrc), .PC(ex_mem_1_pc_2), .PC_2(mem_wb_1_pc_2));
  Adder #(.width(32)) adder_3 (.a(32'h4), .b(mem_wb_1_pc_2), .out(WBPCPlus4));  // open: cin, cout
  Multiplexer #(.select(2), .width(32), .enable("false")) multiplexer_12 (
    .in0(mem_wb_1_aluoutput_2), .in1(mem_wb_1_dataoutput_2), .in2(WBPCPlus4), .out(WriteData),
    .sel(WriteDataSrc));  // open: in3
  // Probe on WriteData

  // Notes on the sheet:
  //   Jal,Jalr
  //   Branches
  //   PCNext
  //   {PCTargetAddress[31:1],1'b0}
  //   For Jar or Branches it is implicit in B, U and J types
  //   PCPlus4
  //   PC
  //   As Jalr is I-type, to align (at least to halfword, for 16 bits modules) target addres is needed to:
  //   Alineado a word (1:0 = 0)
  //   contents of rom_1 (hex, n*v repeats v):
  //   52503 45a583 a58633 c2a223 2b60063 40b606b3 40d60633 b60a63 4*0 c6f6b3 c6e733
  //   IFIDFlush
  //   IFIDRst
  //   IDPC
  //   IDInstruction
  //   Stall
  //   Flush
  //   ForwardBranchA
  //   PCJumpSrc
  //   Immediate
  //   Rd
  //   Instruction (Rs1, Rs2, Opcode)
  //   Moved Equality test (Branch calculation) from EX to ID
  //   ForwardBranchB
  //   PCTargetAddress
  //   BranchA
  //   Instruction
  //   BranchB
  //   PC
  //   EXReadData1
  //   EXReadData2
  //   EXImmediate
  //   Datapath: No Pipeline Identificator means the signal is created in that segment
  //   Pipeline Identificator placed before name
  //   Control: No Pipeline Identificator means signal is used in that segment
  //   Pipeline Identificator placed after name
  //   ALUA
  //   ALUB
  //   PC
  //   ALUBranch
  //   ALUOutput
  //   ReadData2Forw
  //   MEMALUOutput
  //   Branching moved to ID stage
  //   Reduce cost of missprediction
  //   MEMRead or RegWrite -> LOAD
  //   ALUOutput
  //   DataOutput
  //   PC
  //   WBALUOutput
  //   WBDataOutput
  //   ID needs PC, WB needs PCPlus4
  //   WBPCPlus4 can be get in other ways
  //   Old MemtoReg
  //   WriteData
endmodule

module Main_Control (
  input  [31:0] Instruction,
  output ALUSrc,
  output PCJumpSrc,
  output [1:0] WriteDataSrc,
  output RegWrite,
  output MemRead,
  output MemWrite,
  output DoJump,
  output [1:0] LuiAuipcSel,
  output [2:0] StoreLoadSel,
  output [4:0] ALUCtrl
);

  wire lw_out, or_1_out, or_2_out, sw_out;
  wire [1:0] beq_out;
  wire [6:0] undriven;

  and R (beq_out[1], ~undriven[6], undriven[5], undriven[4], ~undriven[3], ~undriven[2], undriven[1], undriven[0]);  // AND_Gate
  and lw (lw_out, ~undriven[6], ~undriven[5], ~undriven[4], ~undriven[3], ~undriven[2], undriven[1], undriven[0]);  // AND_Gate
  and sw (sw_out, ~undriven[6], undriven[5], ~undriven[4], ~undriven[3], ~undriven[2], undriven[1], undriven[0]);  // AND_Gate
  and beq (beq_out[0], undriven[6], undriven[5], ~undriven[4], ~undriven[3], ~undriven[2], undriven[1], undriven[0]);  // AND_Gate
  or or_1 (or_1_out, lw_out, sw_out);
  or or_2 (or_2_out, beq_out[1], lw_out);

  // Notes on the sheet:
  //   Opcode
  //   func3
  //   func7
endmodule

module Register_File (
  input  [4:0] Rs1,
  input  [4:0] Rs2,
  input  WriteEn,
  input  [4:0] Rd,
  input  [31:0] WriteData,
  input  clk,
  input  rst,
  output [31:0] ReadData1,
  output [31:0] ReadData2
);

  wire [15:0] decoder_1_out0, decoder_1_out16;
  wire [31:0] x1___ra_q, x2___sp_q, x3___gp_q, x4___tp_q, x5___t0_q, x6___t1_q, x7___t2_q, x8___s0___fp_q,
       x9___s1_q, x10___a0_q, x11___a1_q, x12___a2_q, x13___a3_q, x14___a4_q, x15___a5_q, x16___a6_q,
       x17___a7_q, x18___s2_q, x19___s3_q, x20___s4_q, x21___s5_q, x22___s6_q, x23___s7_q, x24___s8_q,
       x25___s9_q, x26___s10_q, x27___s11_q, x28___t3_q, x29___t4_q, x30___t5_q, x31___t6_q;

  Decoder #(.select(5), .disabled(0)) decoder_1 (
    .out0(decoder_1_out0[0]), .out1(decoder_1_out0[1]), .out2(decoder_1_out0[2]), .out3(decoder_1_out0[3]),
    .out4(decoder_1_out0[4]), .out5(decoder_1_out0[5]), .out6(decoder_1_out0[6]), .out7(decoder_1_out0[7]),
    .out8(decoder_1_out0[8]), .out9(decoder_1_out0[9]), .out10(decoder_1_out0[10]),
    .out11(decoder_1_out0[11]), .out12(decoder_1_out0[12]), .out13(decoder_1_out0[13]),
    .out14(decoder_1_out0[14]), .out15(decoder_1_out0[15]), .out16(decoder_1_out16[0]),
    .out17(decoder_1_out16[1]), .out18(decoder_1_out16[2]), .out19(decoder_1_out16[3]),
    .out20(decoder_1_out16[4]), .out21(decoder_1_out16[5]), .out22(decoder_1_out16[6]),
    .out23(decoder_1_out16[7]), .out24(decoder_1_out16[8]), .out25(decoder_1_out16[9]),
    .out26(decoder_1_out16[10]), .out27(decoder_1_out16[11]), .out28(decoder_1_out16[12]),
    .out29(decoder_1_out16[13]), .out30(decoder_1_out16[14]), .out31(decoder_1_out16[15]), .sel(Rd),
    .en(WriteEn));
  // Probe on decoder_1_out0
  // Probe on Rd
  Register #(.width(32)) x1___ra (.D(WriteData), .en(decoder_1_out0[1]), .Q(x1___ra_q), .clk(clk), .clr(rst));
  Register #(.width(32)) x2___sp (.D(WriteData), .en(decoder_1_out0[2]), .Q(x2___sp_q), .clk(clk), .clr(rst));
  Register #(.width(32)) x3___gp (.D(WriteData), .en(decoder_1_out0[3]), .Q(x3___gp_q), .clk(clk), .clr(rst));
  Register #(.width(32)) x4___tp (.D(WriteData), .en(decoder_1_out0[4]), .Q(x4___tp_q), .clk(clk), .clr(rst));
  Register #(.width(32)) x5___t0 (.D(WriteData), .en(decoder_1_out0[5]), .Q(x5___t0_q), .clk(clk), .clr(rst));
  Register #(.width(32)) x6___t1 (.D(WriteData), .en(decoder_1_out0[6]), .Q(x6___t1_q), .clk(clk), .clr(rst));
  Register #(.width(32)) x7___t2 (.D(WriteData), .en(decoder_1_out0[7]), .Q(x7___t2_q), .clk(clk), .clr(rst));
  Register #(.width(32)) x8___s0___fp (.D(WriteData), .en(decoder_1_out0[8]), .Q(x8___s0___fp_q), .clk(clk), .clr(rst));
  Register #(.width(32)) x9___s1 (.D(WriteData), .en(decoder_1_out0[9]), .Q(x9___s1_q), .clk(clk), .clr(rst));
  Register #(.width(32)) x10___a0 (.D(WriteData), .en(decoder_1_out0[10]), .Q(x10___a0_q), .clk(clk), .clr(rst));
  Register #(.width(32)) x11___a1 (.D(WriteData), .en(decoder_1_out0[11]), .Q(x11___a1_q), .clk(clk), .clr(rst));
  Register #(.width(32)) x12___a2 (.D(WriteData), .en(decoder_1_out0[12]), .Q(x12___a2_q), .clk(clk), .clr(rst));
  Register #(.width(32)) x13___a3 (.D(WriteData), .en(decoder_1_out0[13]), .Q(x13___a3_q), .clk(clk), .clr(rst));
  Register #(.width(32)) x14___a4 (.D(WriteData), .en(decoder_1_out0[14]), .Q(x14___a4_q), .clk(clk), .clr(rst));
  Register #(.width(32)) x15___a5 (.D(WriteData), .en(decoder_1_out0[15]), .Q(x15___a5_q), .clk(clk), .clr(rst));
  // Probe on x13___a3_q
  Register #(.width(32)) x16___a6 (.D(WriteData), .en(decoder_1_out16[0]), .Q(x16___a6_q), .clk(clk), .clr(rst));
  Register #(.width(32)) x17___a7 (.D(WriteData), .en(decoder_1_out16[1]), .Q(x17___a7_q), .clk(clk), .clr(rst));
  Register #(.width(32)) x18___s2 (.D(WriteData), .en(decoder_1_out16[2]), .Q(x18___s2_q), .clk(clk), .clr(rst));
  Register #(.width(32)) x19___s3 (.D(WriteData), .en(decoder_1_out16[3]), .Q(x19___s3_q), .clk(clk), .clr(rst));
  Register #(.width(32)) x20___s4 (.D(WriteData), .en(decoder_1_out16[4]), .Q(x20___s4_q), .clk(clk), .clr(rst));
  Register #(.width(32)) x21___s5 (.D(WriteData), .en(decoder_1_out16[5]), .Q(x21___s5_q), .clk(clk), .clr(rst));
  Register #(.width(32)) x22___s6 (.D(WriteData), .en(decoder_1_out16[6]), .Q(x22___s6_q), .clk(clk), .clr(rst));
  Register #(.width(32)) x23___s7 (.D(WriteData), .en(decoder_1_out16[7]), .Q(x23___s7_q), .clk(clk), .clr(rst));
  Register #(.width(32)) x24___s8 (.D(WriteData), .en(decoder_1_out16[8]), .Q(x24___s8_q), .clk(clk), .clr(rst));
  Register #(.width(32)) x25___s9 (.D(WriteData), .en(decoder_1_out16[9]), .Q(x25___s9_q), .clk(clk), .clr(rst));
  Register #(.width(32)) x26___s10 (.D(WriteData), .en(decoder_1_out16[10]), .Q(x26___s10_q), .clk(clk), .clr(rst));
  Register #(.width(32)) x27___s11 (.D(WriteData), .en(decoder_1_out16[11]), .Q(x27___s11_q), .clk(clk), .clr(rst));
  Register #(.width(32)) x28___t3 (.D(WriteData), .en(decoder_1_out16[12]), .Q(x28___t3_q), .clk(clk), .clr(rst));
  Register #(.width(32)) x29___t4 (.D(WriteData), .en(decoder_1_out16[13]), .Q(x29___t4_q), .clk(clk), .clr(rst));
  Register #(.width(32)) x30___t5 (.D(WriteData), .en(decoder_1_out16[14]), .Q(x30___t5_q), .clk(clk), .clr(rst));
  Register #(.width(32)) x31___t6 (.D(WriteData), .en(decoder_1_out16[15]), .Q(x31___t6_q), .clk(clk), .clr(rst));
  Multiplexer #(.select(5), .width(32), .enable("false")) multiplexer_1 (
    .in0({32{1'b0}}), .in1(x1___ra_q), .in2(x2___sp_q), .in3(x3___gp_q), .in4(x4___tp_q), .in5(x5___t0_q),
    .in6(x6___t1_q), .in7(x7___t2_q), .in8(x8___s0___fp_q), .in9(x9___s1_q), .in10(x10___a0_q),
    .in11(x11___a1_q), .in12(x12___a2_q), .in13(x13___a3_q), .in14(x14___a4_q), .in15(x15___a5_q),
    .in16(x16___a6_q), .in17(x17___a7_q), .in18(x18___s2_q), .in19(x19___s3_q), .in20(x20___s4_q),
    .in21(x21___s5_q), .in22(x22___s6_q), .in23(x23___s7_q), .in24(x24___s8_q), .in25(x25___s9_q),
    .in26(x26___s10_q), .in27(x27___s11_q), .in28(x28___t3_q), .in29(x29___t4_q), .in30(x30___t5_q),
    .in31(x31___t6_q), .out(ReadData1), .sel(Rs1));
  Multiplexer #(.select(5), .width(32), .enable("false")) multiplexer_2 (
    .in0({32{1'b0}}), .in1(x1___ra_q), .in2(x2___sp_q), .in3(x3___gp_q), .in4(x4___tp_q), .in5(x5___t0_q),
    .in6(x6___t1_q), .in7(x7___t2_q), .in8(x8___s0___fp_q), .in9(x9___s1_q), .in10(x10___a0_q),
    .in11(x11___a1_q), .in12(x12___a2_q), .in13(x13___a3_q), .in14(x14___a4_q), .in15(x15___a5_q),
    .in16(x16___a6_q), .in17(x17___a7_q), .in18(x18___s2_q), .in19(x19___s3_q), .in20(x20___s4_q),
    .in21(x21___s5_q), .in22(x22___s6_q), .in23(x23___s7_q), .in24(x24___s8_q), .in25(x25___s9_q),
    .in26(x26___s10_q), .in27(x27___s11_q), .in28(x28___t3_q), .in29(x29___t4_q), .in30(x30___t5_q),
    .in31(x31___t6_q), .out(ReadData2), .sel(Rs2));

  // Notes on the sheet:
  //   WriteReg
  //   If not not-floating,
  //   when disabled, it can lead to
  //   write all regs
  //   x0 - zero
endmodule

module ALU_Abstraction (
  input  [31:0] ALUA,
  input  [31:0] ALUB,
  input  [4:0] ALUCtrl,
  output [31:0] ALUOutput,
  output Branch
);

  wire comparator_3_gt, comparator_4_eq, comparator_4_lt;
  wire [0:0] beq, bge, bgeu, blt, bltu, bne, sltu;
  wire [31:0] add, \and , \or , sll, slt, sra, srl, sub, undriven, \xor ;

  Adder #(.width(32)) adder_1 (.a(ALUA), .b(ALUB), .out(add));  // open: cin, cout
  Subtractor #(.width(32)) subtractor_1 (.a(ALUA), .b(ALUB), .out(sub));  // open: bin, bout
  Shifter #(.width(32)) shifter_1 (.in(ALUA), .\dist (ALUB[4:0]), .out(sll));
  Comparator #(.width(32)) comparator_1 (.a(ALUA), .b(ALUB), .lt(slt[0]));  // open: gt, eq
  Comparator #(.width(32), .mode("unsigned")) comparator_2 (.a(ALUA), .b(ALUB), .lt(sltu[0]));  // open: gt, eq
  assign \xor  = ALUA ^ ALUB;  // XOR_Gate xor_1, 32 bits wide
  Shifter #(.width(32), .shift("lr")) shifter_2 (.in(ALUA), .\dist (ALUB[4:0]), .out(srl));
  Shifter #(.width(32), .shift("ar")) shifter_3 (.in(ALUA), .\dist (ALUB[4:0]), .out(sra));
  assign \or  = ALUA | ALUB;  // OR_Gate or_1, 32 bits wide
  assign \and  = ALUA & ALUB;  // AND_Gate and_1, 32 bits wide
  Comparator #(.width(32)) comparator_3 (.a(ALUA), .b(ALUB), .gt(comparator_3_gt), .eq(beq[0]), .lt(blt[0]));
  Comparator #(.width(32), .mode("unsigned")) comparator_4 (
    .a(ALUA), .b(ALUB), .gt(bltu[0]), .eq(comparator_4_eq), .lt(comparator_4_lt));
  not not_1 (bne[0], beq[0]);
  or or_2 (bge[0], comparator_3_gt, beq[0]);
  or or_3 (bgeu[0], bltu[0], comparator_4_eq);
  Multiplexer #(.select(5), .width(32), .enable("false")) multiplexer_1 (
    .in0(add), .in1(sub), .in2(sll), .in3(slt), .in4(undriven), .in5(\xor ), .in6(srl), .in7(sra),
    .in8(\or ), .in9(\and ), .out(ALUOutput), .sel(ALUCtrl));  // open: in10, in11, in12, in13, in14, in15, in16, in17, in18, in19, in20, in21, in22, in23, in24, in25, in26, in27, in28, in29, in30, in31

  assign Branch = ALUOutput[0];

  // Notes on the sheet:
  //   add, addi
  //   sub
  //   sll
  //   slt, slti
  //   sltu, sltiu
  //   xor, xori
  //   srl, srli
  //   sra, srai
  //   or, ori
  //   and, andi
  //   Signed
  //   Unsigned
  //   beq
  //   bne
  //   blt
  //   bge
  //   bltu
  //   bgeu
endmodule

module Branch_ALU (
  input  [31:0] BranchA,
  input  [31:0] BranchB,
  input  [4:0] ALUCtrl,
  output BranchALUOutput
);

  wire comparator_1_gt, comparator_2_eq, comparator_2_lt;
  wire [31:0] beq, bge, bgeu, blt, bltu, bne;
  wire [31:1] multiplexer_1_out;

  Comparator #(.width(32)) comparator_1 (.a(BranchA), .b(BranchB), .gt(comparator_1_gt), .eq(beq[0]), .lt(blt[0]));
  Comparator #(.width(32), .mode("unsigned")) comparator_2 (
    .a(BranchA), .b(BranchB), .gt(bltu[0]), .eq(comparator_2_eq), .lt(comparator_2_lt));
  not not_1 (bne[0], beq[0]);
  or or_1 (bge[0], comparator_1_gt, beq[0]);
  or or_2 (bgeu[0], bltu[0], comparator_2_eq);
  Multiplexer #(.select(5), .width(32), .enable("false")) multiplexer_1 (
    .in26(beq), .in27(bne), .in28(blt), .in29(bge), .in30(bltu), .in31(bgeu),
    .out({multiplexer_1_out, BranchALUOutput}), .sel(ALUCtrl));  // open: in0, in1, in2, in3, in4, in5, in6, in7, in8, in9, in10, in11, in12, in13, in14, in15, in16, in17, in18, in19, in20, in21, in22, in23, in24, in25

  // Notes on the sheet:
  //   Signed
  //   Unsigned
  //   beq
  //   bne
  //   blt
  //   bge
  //   bltu
  //   bgeu
endmodule

module ImmGen (
  input  [31:0] Instruction,
  output [31:0] Immediate
);

  wire [31:0] bit_extender_1_out, Btype, Itype, Jtype, shifter_1_out, Stype;

  Bit_Extender #(.in_width(20), .out_width(32), .\type ("sign")) bit_extender_1 (.out(bit_extender_1_out));  // open: in
  Shifter #(.width(32)) shifter_1 (.in(bit_extender_1_out), .\dist (5'b01100), .out(shifter_1_out));
  assign Stype = {{20{Instruction[31]}}, {Instruction[31:25], Instruction[11:7]}};  // Bit_Extender bit_extender_2
  assign Btype = {{19{Instruction[31]}}, {Instruction[31], Instruction[7], Instruction[30:25], Instruction[11:8], 1'b0}};  // Bit_Extender bit_extender_3
  assign Jtype = {{11{Instruction[31]}}, {Instruction[31], Instruction[19:12], Instruction[20], Instruction[30:21], 1'b0}};  // Bit_Extender bit_extender_4
  assign Itype = {{20{Instruction[31]}}, Instruction[31:20]};  // Bit_Extender bit_extender_5
  // Probe on Stype
  // Probe on Btype
  // Probe on {Instruction[31:12], {12{1'b0}}}
  // Probe on Jtype
  // Probe on Itype
  Multiplexer #(.select(5), .width(32), .enable("false")) multiplexer_1 (
    .in0(Itype), .in3(Itype), .in4(Itype), .in5({Instruction[31:12], {12{1'b0}}}), .in8(Stype),
    .in13({Instruction[31:12], {12{1'b0}}}), .in24(Btype), .in25(Itype), .in27(Jtype), .in28(Itype),
    .out(Immediate), .sel(Instruction[6:2]));  // open: in1, in2, in6, in7, in9, in10, in11, in12, in14, in15, in16, in17, in18, in19, in20, in21, in22, in23, in26, in29, in30, in31
  // Probe on Instruction[6:2]

  // Other names for the same wires on the sheet: Utype[31:12] = Instruction[31:12]

  // Notes on the sheet:
  //   "Sign Extend" [19:0] = 0
  //   Calculate all posibilities of immediates and select one of them based on opcode
  //   Use control lines to implement what of the immediates is being to be generated
  //   From this 2 options the second one seems to increment the complexity of the desing while the first one don't implicitly reduces its performance
  //   Bits 2-6 of opcode
  //   Loads
  //   fence
  //   Arithmetics
  //   aupic
  //   Stores
  //   lui
  //   Branches
  //   jalr
  //   jal
  //   ecall/ebreak
endmodule

module IF_ID (
  input  clk,
  input  rst,
  input  en,
  input  [31:0] PC,
  input  [31:0] Instruction,
  output [31:0] PC_2,
  output [31:0] Instruction_2
);

  Register #(.width(32)) register_1 (.D(PC), .en(en), .Q(PC_2), .clk(clk), .clr(rst));
  Register #(.width(32)) register_2 (.D(Instruction), .en(en), .Q(Instruction_2), .clk(clk), .clr(rst));
endmodule

module ID_EX (
  input  clk,
  input  rst,
  input  [31:0] PC,
  input  RegWrite,
  input  [1:0] WriteDataSrc,
  input  [31:0] ReadData1,
  input  [2:0] StoreLoadSel,
  input  [31:0] ReadData2,
  input  MemWrite,
  input  [31:0] Immediate,
  input  MemRead,
  input  [31:0] Instruction,
  input  ALUSrc,
  input  [4:0] Rd,
  input  [1:0] LuiAuipcSel,
  input  [4:0] ReadDir1,
  input  [4:0] ALUCtrl,
  input  [4:0] ReadDir2,
  output [31:0] PC_2,
  output RegWrite_2,
  output [1:0] WriteDataSrc_2,
  output [31:0] ReadData1_2,
  output [2:0] StoreLoadSel_2,
  output [31:0] ReadData2_2,
  output MemWrite_2,
  output [31:0] Immediate_2,
  output MemRead_2,
  output [31:0] Instruction_2,
  output ALUSrc_2,
  output [4:0] Rd_2,
  output [1:0] LuiAuipcSel_2,
  output [4:0] ReadDir1_2,
  output [4:0] ALUCtrl_2,
  output [4:0] ReadDir2_2
);

  Register #(.width(32)) register_1 (.D(PC), .Q(PC_2), .clk(clk), .clr(rst));  // open: en
  Register #(.width(32)) register_2 (.D(ReadData1), .Q(ReadData1_2), .clk(clk), .clr(rst));  // open: en
  Register #(.width(32)) register_3 (.D(ReadData2), .Q(ReadData2_2), .clk(clk), .clr(rst));  // open: en
  Register #(.width(32)) register_4 (.D(Immediate), .Q(Immediate_2), .clk(clk), .clr(rst));  // open: en
  Register #(.width(32)) register_5 (.D(Instruction), .Q(Instruction_2), .clk(clk), .clr(rst));  // open: en
  Register #(.width(5)) register_6 (.D(Rd), .Q(Rd_2), .clk(clk), .clr(rst));  // open: en
  Register #(.width(5)) register_7 (.D(ReadDir1), .Q(ReadDir1_2), .clk(clk), .clr(rst));  // open: en
  Register #(.width(5)) register_8 (.D(ReadDir2), .Q(ReadDir2_2), .clk(clk), .clr(rst));  // open: en
  Register #(.width(1)) register_9 (.D(RegWrite), .Q(RegWrite_2), .clk(clk), .clr(rst));  // open: en
  Register #(.width(2)) register_10 (.D(WriteDataSrc), .Q(WriteDataSrc_2), .clk(clk), .clr(rst));  // open: en
  Register #(.width(3)) u_StoreLoadSel (.D(StoreLoadSel), .Q(StoreLoadSel_2), .clk(clk), .clr(rst));  // open: en
  Register #(.width(1)) register_11 (.D(MemWrite), .Q(MemWrite_2), .clk(clk), .clr(rst));  // open: en
  Register #(.width(1)) register_12 (.D(MemRead), .Q(MemRead_2), .clk(clk), .clr(rst));  // open: en
  Register #(.width(1)) register_13 (.D(ALUSrc), .Q(ALUSrc_2), .clk(clk), .clr(rst));  // open: en
  Register #(.width(2)) register_14 (.D(LuiAuipcSel), .Q(LuiAuipcSel_2), .clk(clk), .clr(rst));  // open: en
  Register #(.width(5)) register_15 (.D(ALUCtrl), .Q(ALUCtrl_2), .clk(clk), .clr(rst));  // open: en

  // Notes on the sheet:
  //   DATAPATH
  //   FORWARDING
  //   CONTROL
  //   WB
  //   MEM
  //   EX
endmodule

module EX_MEM (
  input  clk,
  input  rst,
  input  [31:0] PC,
  input  RegWrite,
  input  [1:0] WriteDataSrc,
  input  Zero,
  input  [31:0] ALUOutput,
  input  [2:0] StoreLoadSel,
  input  MemWrite,
  input  [31:0] ReadData2,
  input  MemRead,
  input  [4:0] Rd,
  output [31:0] PC_2,
  output RegWrite_2,
  output [1:0] WriteDataSrc_2,
  output Zero_2,
  output [31:0] ALUOutput_2,
  output [2:0] StoreLoadSel_2,
  output MemWrite_2,
  output [31:0] ReadData2_2,
  output MemRead_2,
  output [4:0] Rd_2
);

  Register #(.width(32)) register_1 (.D(PC), .Q(PC_2), .clk(clk), .clr(rst));  // open: en
  Register #(.width(1)) register_2 (.D(Zero), .Q(Zero_2), .clk(clk), .clr(rst));  // open: en
  Register #(.width(32)) register_3 (.D(ALUOutput), .Q(ALUOutput_2), .clk(clk), .clr(rst));  // open: en
  Register #(.width(32)) register_4 (.D(ReadData2), .Q(ReadData2_2), .clk(clk), .clr(rst));  // open: en
  Register #(.width(5)) register_5 (.D(Rd), .Q(Rd_2), .clk(clk), .clr(rst));  // open: en
  Register #(.width(1)) register_6 (.D(RegWrite), .Q(RegWrite_2), .clk(clk), .clr(rst));  // open: en
  Register #(.width(2)) register_7 (.D(WriteDataSrc), .Q(WriteDataSrc_2), .clk(clk), .clr(rst));  // open: en
  Register #(.width(3)) u_StoreLoadSel (.D(StoreLoadSel), .Q(StoreLoadSel_2), .clk(clk), .clr(rst));  // open: en
  Register #(.width(1)) register_8 (.D(MemWrite), .Q(MemWrite_2), .clk(clk), .clr(rst));  // open: en
  Register #(.width(1)) register_9 (.D(MemRead), .Q(MemRead_2), .clk(clk), .clr(rst));  // open: en

  // Notes on the sheet:
  //   DATAPATH
  //   CONTROL
  //   WB
  //   MEM
endmodule

module MEM_WB (
  input  clk,
  input  rst,
  input  [31:0] PC,
  input  RegWrite,
  input  [1:0] WriteDataSrc,
  input  [31:0] ALUOutput,
  input  [31:0] DataOutput,
  input  [4:0] WriteDir,
  output [31:0] PC_2,
  output RegWrite_2,
  output [1:0] WriteDataSrc_2,
  output [31:0] ALUOutput_2,
  output [31:0] DataOutput_2,
  output [4:0] WriteDir_2
);

  Register #(.width(32)) register_1 (.D(PC), .Q(PC_2), .clk(clk), .clr(rst));  // open: en
  Register #(.width(32)) register_2 (.D(ALUOutput), .Q(ALUOutput_2), .clk(clk), .clr(rst));  // open: en
  Register #(.width(32)) register_3 (.D(DataOutput), .Q(DataOutput_2), .clk(clk), .clr(rst));  // open: en
  Register #(.width(5)) register_4 (.D(WriteDir), .Q(WriteDir_2), .clk(clk), .clr(rst));  // open: en
  Register #(.width(1)) register_5 (.D(RegWrite), .Q(RegWrite_2), .clk(clk), .clr(rst));  // open: en
  Register #(.width(2)) register_6 (.D(WriteDataSrc), .Q(WriteDataSrc_2), .clk(clk), .clr(rst));  // open: en

  // Notes on the sheet:
  //   DATAPATH
  //   CONTROL
  //   WB
endmodule

module Forwarding (
  input  [4:0] Rs1,
  input  [4:0] Rs2,
  input  [4:0] MEMRd,
  input  [4:0] WBRd,
  input  RegWriteMEM,
  input  RegWrite,
  output [1:0] ForwardA,
  output [1:0] ForwardB
);
endmodule

module Hazard_Detection (
  input  [31:0] Instruction,
  input  MemReadEX,
  input  RegWriteEX,
  input  MemRead,
  input  [4:0] EXRd,
  input  [4:0] MEMRd,
  input  BranchID,
  input  PCSrc,
  output PCWrite,
  output IFIDWrite,
  output Stall,
  output IFIDFlush
);


  // Notes on the sheet:
  //   STALL
  //   FLUSH
  //   ALU Stall
  //   BranchALU Stall: RTYPE or LOAD
  //   ALU depends on load data, stall for one cycle using MemReadEX
  //   Uses both MemRead to stall 2 cycles for a load, then forwarding.
  //   La idea es implementar la instrucción nop y en el caso de que se deba producir una bubble, detener la escritura ENABLE del PC y IFIDreg y sustituir la instrucción por un NOP
  //   Mala opción usar un nop como stall. Razón word bibliografía.
  //   STALL
  //   FLUSH
endmodule

module Load (
  input  [1:0] DataType,
  input  [1:0] AluOutput,
  input  Unsigned,
  input  [31:0] Data,
  output [31:0] FixedData
);

  wire [7:0] multiplexer_1_out;
  wire [15:0] multiplexer_2_out;
  wire [31:0] bit_extender_1_out, bit_extender_2_out, bit_extender_3_out, bit_extender_4_out, Byte, Half;

  Multiplexer #(.select(2), .width(8), .enable("false")) multiplexer_1 (
    .in0(Data[7:0]), .in1(Data[15:8]), .in2(Data[23:16]), .in3(Data[31:24]), .out(multiplexer_1_out),
    .sel(AluOutput));
  Multiplexer #(.width(16), .enable("false")) multiplexer_2 (
    .in0(Data[15:0]), .in1(Data[31:16]), .out(multiplexer_2_out), .sel(AluOutput[1]));
  assign bit_extender_1_out = {{24{multiplexer_1_out[7]}}, multiplexer_1_out};  // Bit_Extender bit_extender_1
  assign bit_extender_2_out = {{24{1'b0}}, multiplexer_1_out};  // Bit_Extender bit_extender_2
  assign bit_extender_3_out = {{16{multiplexer_2_out[15]}}, multiplexer_2_out};  // Bit_Extender bit_extender_3
  assign bit_extender_4_out = {{16{1'b0}}, multiplexer_2_out};  // Bit_Extender bit_extender_4
  Multiplexer #(.width(32), .enable("false")) multiplexer_3 (
    .in0(bit_extender_1_out), .in1(bit_extender_2_out), .out(Byte), .sel(Unsigned));
  Multiplexer #(.width(32), .enable("false")) multiplexer_4 (
    .in0(bit_extender_3_out), .in1(bit_extender_4_out), .out(Half), .sel(Unsigned));
  Multiplexer #(.select(2), .width(32), .enable("false")) multiplexer_5 (
    .in0(Byte), .in1(Half), .in2(Data), .out(FixedData), .sel(DataType));  // open: in3

  // Other names for the same wires on the sheet: Word[31:0] = Data

  // Notes on the sheet:
  //   Byte0
  //   Byte1
  //   Byte2
  //   Byte3
  //   Half0
  //   Half1
  //   Word
  //   Ordered based on func3 for Load Opcode
  //   = Func3[1:0]
endmodule

module Store (
  input  [1:0] DataType,
  input  [31:0] Data,
  input  [1:0] AluOutput,
  output [31:0] FixedData,
  output [3:0] MemoryByteSel
);

  wire [3:0] ByteSelByte, ByteSelHalf;
  wire [7:0] multiplexer_1_out;
  wire [15:0] multiplexer_2_out;
  wire [31:0] Byte, Half;

  Multiplexer #(.select(2), .width(8), .enable("false")) multiplexer_1 (
    .in0(Data[7:0]), .in1(Data[15:8]), .in2(Data[23:16]), .in3(Data[31:24]), .out(multiplexer_1_out),
    .sel(AluOutput));
  Multiplexer #(.width(16), .enable("false")) multiplexer_2 (
    .in0(Data[15:0]), .in1(Data[31:16]), .out(multiplexer_2_out), .sel(AluOutput[1]));
  Multiplexer #(.select(2), .width(4), .enable("false")) multiplexer_3 (
    .in0(4'b0001), .in1(4'b0010), .in2(4'b0100), .in3(4'b1000), .out(ByteSelByte), .sel(AluOutput));
  Multiplexer #(.width(4), .enable("false")) multiplexer_4 (
    .in0(4'b0011), .in1(4'b1100), .out(ByteSelHalf), .sel(AluOutput[1]));
  assign Byte = {{24{1'b0}}, multiplexer_1_out};  // Bit_Extender bit_extender_1
  assign Half = {{16{1'b0}}, multiplexer_2_out};  // Bit_Extender bit_extender_2
  Multiplexer #(.select(2), .width(32), .enable("false")) multiplexer_5 (
    .in0(Byte), .in1(Half), .in2(Data), .out(FixedData), .sel(DataType));  // open: in3
  Multiplexer #(.select(2), .width(4), .enable("false")) multiplexer_6 (
    .in0(ByteSelByte), .in1(ByteSelHalf), .in2(4'b1111), .out(MemoryByteSel), .sel(DataType));  // open: in3

  // Other names for the same wires on the sheet: Word[31:0] = Data

  // Notes on the sheet:
  //   Byte0
  //   Byte1
  //   Byte2
  //   Byte3
  //   Half0
  //   Half1
  //   Word
  //   Ordered based on func3 for Load Opcode
  //   = Func3[1:0]
endmodule

module AddrAlignment (
  input  [31:0] ALUOutput,
  input  [1:0] AlignmentSel,
  output [7:0] Dir
);

  wire [7:0] HalfAlign;

  Multiplexer #(.select(2), .width(8), .disabled(0), .enable("false")) multiplexer_1 (
    .in0(ALUOutput[7:0]), .in1(HalfAlign), .in2({ALUOutput[7:2], 2'b00}), .out(Dir), .sel(AlignmentSel));  // open: in3

  // Other names for the same wires on the sheet: ByteAlign[7:0] = ALUOutput[7:0]; WordAlign[7:2] = ALUOutput[7:2]

  // Notes on the sheet:
  //   = func3[1:0]
endmodule
